# Fritzing sketch SensorIR (saved by Fritzing 0.9.3b)
breadboards: 1

parts:
  Componente1 = BlackBoard
  IR1 = TSOP312.., 314.. [package=THT]
  LED1 = LED - 5mm [color="Red (633nm)" package="5 mm [THT]"]
  LED2 = LED - 5mm [color="Yellow (592nm)" package="5 mm [THT]"]
  LED3 = LED - 5mm [color="Green (570nm)" package="5 mm [THT]"]
  LED4 = LED - 5mm [color="White (6500K)" package="5 mm [THT]"]
  R1 = Resistor [tolerance=±5% resistance=1k package=THT]
  R2 = Resistor [tolerance=±5% resistance=330 package=THT]
  R3 = Resistor [tolerance=±5% resistance=1k package=THT]
  R4 = Resistor [tolerance=±5% resistance=1k package=THT]

nets:
  N1: Componente1.pin_4, IR1.Vs
  N2: Componente1.pin_6, IR1.GND
  N3: Componente1.pin_23, R4.Pin_0
  N4: Componente1.pin_24, R3.Pin_0
  N5: Componente1.pin_25, R2.Pin_0
  N6: Componente1.pin_26, R1.Pin_0
  N7: LED1.anode, R1.Pin_1
  N8: LED2.anode, R2.Pin_1
  N9: LED3.anode, R3.Pin_1
  N10: LED4.anode, R4.Pin_1

custom parts:
  BlackBoard: The Arduino Uno is a microcontroller board based on the ATmega328 (datasheet). It has 14 digital input/output pins (of which 6 can be used as PWM outputs), 6 analog inputs, a 16 MHz ceramic resonator, a USB connection, a power jack, an ICSP header, and a reset button. It contains everything needed to support the microcontroller; simply connect it to a computer with a USB cable or power it with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

// code stored in the sketch: SensorIR.ino
#include <IRremote.h>
#include <IRremoteInt.h>

const int leds[] = {9, 10, 11, 12};
const int IR = 8;
float armazenaValor;

IRrecv irrecv(IR);
decode_results results;

void setup() {
  for(int i = 0; i <= leds; i++) {
    pinMode(leds[i], OUTPUT);
  }

  Serial.begin(9600);
  irrecv.enableIRIn(); // inicializa o sensor IR
}

void loop() {
  if(irrecv.decode(&results)) {
    Serial.print("Valor lido: ");
    Serial.println(results.value, HEX);
    armazenaValor = results.value;
    irrecv.resume();
    

    if(armazenaValor == 0xF720DF) {
      Serial.println("Led vermelho ligado!");
      digitalWrite(leds[3], HIGH);
    } else if (led2[3] == HIGH) {
			digitalWrite(leds[3], LOW);
		}

    if(armazenaValor == 0xF7A05F) {
      Serial.println("Led verde ligado!");
      digitalWrite(leds[1], HIGH);
    }

    if(armazenaValor == 0xF7E01F) {
      Serial.println("Led branco ligado!");
      digitalWrite(leds[0], HIGH);
    }

    if(armazenaValor == 0xF728D7) {
      Serial.println("Led amarelo ligado!");
      digitalWrite(leds[2], HIGH);
    }

    if(armazenaValor == 0xF740BF) {
      Serial.println("Todos os leds foram desligados");
      for(int i = 0; i <= leds; i++) {
        digitalWrite(leds[i], LOW);
      }
    }
  }
}
