# Fritzing sketch arduino-ntc (saved by Fritzing 0.9.3b)
breadboards: 1

parts:
  Componente1 = Arduino Uno (Rev3)
  R1 = Resistor [tolerance=±5% resistance=10k package=THT]
  R2 = Temperature Sensor (Thermistor) [thermistor_type=NTC package=THT]
  J1 = Piezo Speaker
  K1 = Relay [part_number=FRS1B-S package=THT]  # not connected

nets:
  N1: Componente1.A0, R1.Pin_1, R2.pin_1
  N2: Componente1.D12/MISO, J1.pin2
  N3: Componente1.5V, R2.pin_0
  N4: Componente1.GND, R1.Pin_0, J1.pin1
