# Fritzing sketch car_security (saved by Fritzing 0.9.3b)
breadboards: 1

parts:
  Componente1 = Arduino Pro Mini (5V)
  R1 = Resistor [tolerance=±5% resistance=10k package=THT]
  R2 = Resistor [tolerance=±5% resistance=10k package=THT]
  LED1 = LED - 5mm [color="Red (633nm)" package="5 mm [THT]"]
  LED2 = LED - 5mm [color="Green (570nm)" package="5 mm [THT]"]
  LED3 = LED - 5mm [color="White (8000K)" package="5 mm [THT]"]
  R3 = Resistor [tolerance=±5% resistance=1k package=THT]
  R4 = Resistor [tolerance=±5% resistance=1k package=THT]
  R5 = Resistor [tolerance=±5% resistance=1k package=THT]
  S1 = Pushbutton [package="[THT]"]
  R6 = Resistor [tolerance=±5% resistance=10k package=THT]
  Power_plug1 = Power plug

nets:
  VCC: Componente1.VCC, Componente1.SCK, R1.Pin_1, S1.Pin_3, S1.Pin_4, Power_plug1.VCC
  GND: Componente1.GND, LED1.anode, LED2.anode, LED3.anode, R6.Pin_1, Power_plug1.GND
  N1: Componente1.MISO, R2.Pin_0
  N2: Componente1.MOSI, R4.Pin_1
  N3: Componente1.D10, R3.Pin_1
  N4: Componente1.D9, R5.Pin_1
  N5: R1.Pin_0, R2.Pin_1
  N6: LED1.cathode, R3.Pin_0
  N7: LED2.cathode, R4.Pin_0
  N8: LED3.cathode, R5.Pin_0
  N9: S1.Pin_1, S1.Pin_2, R6.Pin_0
