# Fritzing sketch dec_bin circuit (saved by Fritzing 0.9.3b)
breadboards: 1

parts:
  Componente1 = BlackBoard
  D1 = LED_BARGRAPH_10 [package=led_bargaph_10]
  R1 = Resistor [tolerance=±5% resistance=330 package=THT]

nets:
  N1: Componente1.pin_6, R1.Pin_1
  N2: Componente1.pin_18, D1.J_C
  N3: Componente1.pin_19, D1.I_C
  N4: Componente1.pin_20, D1.H_C
  N5: Componente1.pin_21, D1.G_C
  N6: Componente1.pin_22, D1.F_C
  N7: Componente1.pin_23, D1.E_C
  N8: Componente1.pin_24, D1.D_C
  N9: Componente1.pin_25, D1.C_C
  N10: Componente1.pin_26, D1.B_C
  N11: Componente1.pin_27, D1.A_C
  N12: D1.A_A, D1.B_A, D1.C_A, D1.D_A, D1.E_A, D1.F_A, D1.G_A, D1.H_A, D1.I_A, D1.J_A

custom parts:
  BlackBoard: The Arduino Uno is a microcontroller board based on the ATmega328 (datasheet). It has 14 digital input/output pins (of which 6 can be used as PWM outputs), 6 analog inputs, a 16 MHz ceramic resonator, a USB connection, a power jack, an ICSP header, and a reset button. It contains everything needed to support the microcontroller; simply connect it to a computer with a USB cable or power it with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

// code stored in the sketch: dec_bin.ino
/************************************************************************ 
 *  Código base retirado do site Electro Schematics                     *
 * (http://www.electroschematics.com/9809/arduino-8-bit-binary-led/)    *
 * Código adaptado para se adequar ao uso.                              *
 * Modificações: Wendell Stanley Araújo Rocha                           *
 * Link para o repositório: https://github.com/WendellRocha/Arduino     *
 * Código desponibilizado para ser utilizado e alterado para se adequar *
 * ao seu código.                                                       *
 * Por favor, não retire os créditos.                                   *
 ************************************************************************/

int letra = 0;    // variable to store number of conversoes
const byte numbarra = 10; // número de leds da barra
int state;        // usado para o estado HIGH ou LOW
 // barra de leds
byte barra[] = {4, 5, 6, 7, 8, 9, 10, 11, 12, 13};

void setup() {
  
  for(int i = 0; i < numbarra; i++) {
    pinMode(barra[i], OUTPUT);
  }
  
  Serial.begin(9600);

}

void loop() {
  
  if (Serial.available() > 0) {
    letra = Serial.read();    
  }
  
  String binNumber = String(letra, BIN);
  int binLength = binNumber.length();
  for(int i = 0, x = 1; i < binLength; i++, x+=2) {
    if(binNumber[i] == '0') state = LOW;
    if(binNumber[i] == '1') state = HIGH;
      digitalWrite(barra[i] + binLength - x, state);
    }
}
