# Fritzing sketch semaforo (saved by Fritzing 0.9.3b)
breadboards: 1

parts:
  Componente1 = BlackBoard
  S1 = Pushbutton [package="[THT]"]
  LED1 = LED - 5mm [color="Red (633nm)" package="5 mm [THT]"]
  LED2 = LED - 5mm [color="Yellow (595nm)" package="5 mm [THT]"]
  LED3 = LED - 5mm [color="Green (560nm)" package="5 mm [THT]"]
  LED4 = LED - 5mm [color="Red (633nm)" package="5 mm [THT]"]
  LED5 = LED - 5mm [color="Green (555nm)" package="5 mm [THT]"]
  R1 = Resistor [tolerance=±5% resistance=1k package=THT]
  R2 = Resistor [tolerance=±5% resistance=1k package=THT]
  R3 = Resistor [tolerance=±5% resistance=1k package=THT]
  R4 = Resistor [tolerance=±5% resistance=1k package=THT]
  R5 = Resistor [tolerance=±5% resistance=330 package=THT]
  R6 = Resistor [tolerance=±5% resistance=330 package=THT]

nets:
  N1: Componente1.pin_4, S1.Pin_1, S1.Pin_2
  N2: Componente1.pin_22, S1.Pin_3, S1.Pin_4, R6.Pin_1
  N3: Componente1.pin_23, R2.Pin_1
  N4: Componente1.pin_24, R4.Pin_1
  N5: Componente1.pin_25, R5.Pin_1
  N6: Componente1.pin_26, R3.Pin_1
  N7: Componente1.pin_27, R1.Pin_1
  N8: LED1.cathode, LED2.cathode, LED3.cathode
  N9: LED1.anode, R4.Pin_0
  N10: LED2.anode, R5.Pin_0
  N11: LED3.anode, R3.Pin_0
  N12: LED4.cathode, LED5.cathode, R6.Pin_0
  N13: LED4.anode, R1.Pin_0
  N14: LED5.anode, R2.Pin_0

custom parts:
  BlackBoard: The Arduino Uno is a microcontroller board based on the ATmega328 (datasheet). It has 14 digital input/output pins (of which 6 can be used as PWM outputs), 6 analog inputs, a 16 MHz ceramic resonator, a USB connection, a power jack, an ICSP header, and a reset button. It contains everything needed to support the microcontroller; simply connect it to a computer with a USB cable or power it with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

// code stored in the sketch: semaforo.ino
/* Desafio do semáforo com semáforo para padestres                      *
 * Wendell Rocha, 115210754                                             *
 * Iniciação à Computação, 2015.2                                       *
 * wendell.rocha@ccc.ufcg.edu.br                                        *
 * Feito por: Wendell Stanley Araújo Rocha                              *
 * Link para o repositório: https://github.com/WendellRocha/Arduino     *
 * Código desponibilizado para ser utilizado e alterado para se adequar *
 * ao seu código.                                                       *
 * Por favor, não retire os créditos.                                   *
 ************************************************************************/ 

const int botao = 8; // botão do semáforo no pino 8
const int leds[] = {9, 10, 11, 12, 13}
int estadodobotao = 0; // estado do botão do semáforo

/**
  led verde do pedestre no pino 9
  led vermelho no pino 10
  led amarelo no pino 11
  led verde no pino 12
  led vermelho do pedestre no pino 13
  */


void setup() {
   for(int i = 0; i < 4; i++) {
    pinMode(leds[i], OUTPUT);
  }
  pinMode(botao, INPUT); // pino do botão em modo de entrada

}

void loop() {
 
  estadodobotao = digitalRead(botao); // atribui o valor da leitura do pino do botão ao estadodobotao
  if (estadodobotao == HIGH) { // se o estado do botão for HIGH (alto, 1)
    delay(10000); // inicia uma contagem de 10 segundos    
    digitalWrite(leds[3], LOW); // após a contagem de 10 segundos, apaga o led verde
    digitalWrite(leds[2], HIGH); // após apagar o led vede, acende o amarelo
    delay(5000); // inicia uma contagem de 5 segundos
    digitalWrite(leds[2], LOW); // após a contagem de 5 segundos, apaga o led amarelo
    digitalWrite(leds[4], LOW); // após a contagem de 5 segundos, apaga o led vermelho para o padestre
    digitalWrite(led_red, HIGH); // após a contagem de 5 segundos, acende o led vermelho para os veículos
    delay(750); // delay de segurança para acender o led verde para os pedestres
    digitalWrite(leds[0], HIGH); // após a contagem de 75 milisegundos, acende o led verde para o pedestre
    delay(15000); // inicia uma contagem de 15 segundos

    for (int y = 0; y < 1; y++) { // para y igual a zero; y menor que 1; use y e depois incremente                    /* laço para piscar o led vermelho no final da contagem */
      digitalWrite(leds[1], LOW); // apaga o led vermelho dos veículos
      delay(250); // conta 25 milisegundos
      digitalWrite(leds[3], HIGH); // acende o led vermelho dos veículos
    }
       
    for (int x = 0; x < 10; x++) { // para x igual a zero; x menor que dez; use x e depois incremete                    /* laço para piscar o led vermelho no final da contagem */
      digitalWrite(leds[4], HIGH); // acende o led verde do padestre
      delay(250); // conta 25 milisegundos
      digitalWrite(leds[4], LOW); // apaga o lede verde do padestre
      delay(250); // conta 2,5 segundos
    }
    
    digitalWrite(leds[1], LOW); // após a contagem de 15 segundos, apaga o led vermelho
    digitalWrite(leds[0], LOW); // após a contagem de 15 segundos, apaga o led verde do padestre
      
  }
  else { // senão 
    
     digitalWrite(led_green, HIGH); // assim que o programa iniciar, ligará o led verde para os veículos
     digitalWrite(led_red_ped, HIGH); // assim que o programa iniciar, ligará o led vermelho para o padestre
  }

}
