# Fritzing sketch temperatura (saved by Fritzing 0.9.3b)
breadboards: 1

parts:
  T1 = LM34 Temperature Sensor [package="TO92 [THT]"]
  M1 = DC Motor
  R1 = Resistor [tolerance=±5% resistance=2.2k package=THT]
  C1 = Electrolytic Capacitor [capacitance=100μF voltage=16V package="0807 [SMD, electrolytic]"]
  R2 = Resistor [tolerance=±5% resistance=330 package=THT]
  Q1 = TIP120 Hi-Current Darlington Transistor
  Componente1 = BlackBoard
  JACK1 = 2.1mm DC Barrel Jack

nets:
  N1: T1.+Vs, Componente1.pin_4
  N2: T1.Vout, R2.Pin_0, Componente1.pin_8
  N3: T1.GND, C1.-, R2.Pin_1, Q1.EMITTER, Componente1.pin_5, JACK1.sleeve
  N4: M1.pin_1, Q1.COLLECTOR
  N5: M1.pin_2, JACK1.center
  N6: R1.Pin_0, Componente1.pin_25
  N7: R1.Pin_1, C1.+, Q1.BASE

custom parts:
  BlackBoard: The Arduino Uno is a microcontroller board based on the ATmega328 (datasheet). It has 14 digital input/output pins (of which 6 can be used as PWM outputs), 6 analog inputs, a 16 MHz ceramic resonator, a USB connection, a power jack, an ICSP header, and a reset button. It contains everything needed to support the microcontroller; simply connect it to a computer with a USB cable or power it with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
  2.1mm DC Barrel Jack: 2.1mm DC Barrel Jack with Thru-Hole Connectors (breadboardable)

// code stored in the sketch: temperatura.ino
/************************************************************************
 * Feito por: Wendell Stanley Araújo Rocha                              *
 * Link para o repositório: https://github.com/WendellRocha/Arduino     *
 * Código desponibilizado para ser utilizado e alterado para se adequar *
 * ao seu código.                                                       *
 * Sistema de controle da rotação do cooler de acordo com a temperatura *
 * Por favor, não retire os créditos.                                   *
 ************************************************************************/

const int lm35 = 0;
const int cooler = 11;
int temperatura = 0;
int samples[8];

void setup() {
  Serial.begin(9600);
  pinMode(cooler, OUTPUT);
}

void loop() {
  for (int i = 0; i <= 7; i++) {
    samples[i] = (5.0 * analogRead(lm35) * 100.0) / 1024.0;
    temperatura += samples[i];
    delay(100);
  }

  temperatura /= 8.0;

  if (temperatura > 27.0) {
    analogWrite(cooler, 255);
  }

  else if (temperatura >= 25.0 && temperatura <= 27.0) {
    analogWrite(cooler, 127);
  }

  else {
    analogWrite(cooler, 0);
  }

  Serial.print(temperatura, DEC);
  Serial.print(" Cels. \n");

  temperatura = 0;
  delay(1000);
}
